# Fritzing sketch st7789_rp2040 (saved by Fritzing 1.0.4)
breadboards: 1

parts:
  Adafruit_Color_Newxie_TFT_Display1 = Adafruit Color Newxie TFT Display [part_number=#6113]
  Mod1 = Raspberry Pi Pico

nets:
  N1: Adafruit_Color_Newxie_TFT_Display1.VIN, Mod1.pin_36
  N2: Adafruit_Color_Newxie_TFT_Display1.GND, Mod1.pin_3, Mod1.pin_8, Mod1.pin_13, Mod1.pin_18, Mod1.pin_23, Mod1.pin_28, Mod1.pin_33, Mod1.pin_38
  N3: Adafruit_Color_Newxie_TFT_Display1.SCK, Mod1.pin_4
  N4: Adafruit_Color_Newxie_TFT_Display1.MOSI, Mod1.pin_5
  N5: Adafruit_Color_Newxie_TFT_Display1.TFTCS, Mod1.pin_7
  N6: Adafruit_Color_Newxie_TFT_Display1.DC, Mod1.pin_10
  N7: Adafruit_Color_Newxie_TFT_Display1.BACKLIGHT, Mod1.pin_9

custom parts:
  Adafruit Color Newxie TFT Display: Say hello to our new Newxie 1.14" 240x135 Color TFT Display Boards – we think it's T-F-Terrific! It's the size of your thumbnail, with glorious 240x135 high res pixel color. This very very small display is only 1.14" diagonal, packed with RGB pixels, for making very small high-density displays. And this breakout board is designed for compact 'stacking' on a 0.1" grid - with a vertical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
  Raspberry Pi Pico: Raspberry Pi Pico. Based around the RP2040 microcontroller the Pico is a low cost microcontroller device bringing Raspberry Pi quality, cost, and easy of use to the microcontroller space. Jan 2021, Split part in to two versions: tht (this one) and SMD. This one will drill holes for a .1 in header in pcb to allow plugging in the module as well as providing pads to solder the module to the top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
